// Logisim project GM_16x.circ as structural Verilog: 7 circuits, main circuit main
module main (
  input  in_1
);

  wire alu_1_zero, b, clk, control_logic_1_j, control_logic_1_strreg, j, lw, or_1_out, sw;
  wire [3:0] multiplexer_2_out, multiplexer_2_out_2, multiplexer_2_out_3, multiplexer_2_out_4,
       rom_1_instruction, rom_1_instruction_2, rom_1_instruction_3, rom_1_instruction_4;
  wire [15:0] alu_1_out, demultiplexer_1_out0, demultiplexer_1_out1, mem_1_dataout, multiplexer_1_out,
       regs_1_data1, regs_1_data2, regs_1_jumper;

  Clock clock_1 (.out(clk));
  Multiplexer #(.width(16)) multiplexer_1 (
    .in0({multiplexer_2_out_4, multiplexer_2_out_3, multiplexer_2_out_2, multiplexer_2_out}),
    .in1(regs_1_jumper), .out(multiplexer_1_out), .sel(b));  // open: en
  Control_Logic control_logic_1 (
    .j(control_logic_1_j), .b(b), .ldMem(lw), .strMem(sw), .strReg(control_logic_1_strreg),
    .op(rom_1_instruction_4));
  ROM rom_1 (
    .Address(multiplexer_1_out),
    .Instruction({rom_1_instruction_4, rom_1_instruction_3, rom_1_instruction_2, rom_1_instruction}), .gt(j),
    .clk(clk), .clr(in_1));
  Hex_Digit_Display hex_digit_display_1 (.value(rom_1_instruction_4));  // open: dp
  Regs regs_1 (
    .str(control_logic_1_strreg), .rd(rom_1_instruction_3),
    .in({multiplexer_2_out_4, multiplexer_2_out_3, multiplexer_2_out_2, multiplexer_2_out}),
    .data1(regs_1_data1), .data2(regs_1_data2), .rt(rom_1_instruction), .clk(clk), .clr(in_1),
    .rs(rom_1_instruction_2), .jumper(regs_1_jumper));
  Hex_Digit_Display hex_digit_display_2 (.value(rom_1_instruction_3));  // open: dp
  Hex_Digit_Display hex_digit_display_3 (.value(rom_1_instruction_2));  // open: dp
  Hex_Digit_Display hex_digit_display_4 (.value(multiplexer_1_out[11:8]));  // open: dp
  Hex_Digit_Display hex_digit_display_5 (.value(multiplexer_1_out[15:12]));  // open: dp
  Hex_Digit_Display hex_digit_display_6 (.value(multiplexer_2_out_4));  // open: dp
  Hex_Digit_Display hex_digit_display_7 (.value(multiplexer_2_out_3));  // open: dp
  branch branch_1 (.b(b), .j(control_logic_1_j), .z(alu_1_zero), .j_2(j));
  ALU alu_1 (
    .data1(regs_1_data1), .data2(regs_1_data2),
    .immed({rom_1_instruction_4, rom_1_instruction_3, rom_1_instruction_2, rom_1_instruction}),
    .out(alu_1_out), .zero(alu_1_zero));
  Demultiplexer #(.width(16)) demultiplexer_1 (
    .out0(demultiplexer_1_out0), .out1(demultiplexer_1_out1), .in(alu_1_out), .sel(or_1_out));  // open: en
  or or_1 (or_1_out, sw, lw);
  Multiplexer #(.width(16)) multiplexer_2 (
    .in0(demultiplexer_1_out0), .in1(mem_1_dataout),
    .out({multiplexer_2_out_4, multiplexer_2_out_3, multiplexer_2_out_2, multiplexer_2_out}), .sel(or_1_out));  // open: en
  Hex_Digit_Display hex_digit_display_8 (.value(rom_1_instruction));  // open: dp
  Hex_Digit_Display hex_digit_display_9 (.value(multiplexer_1_out[3:0]));  // open: dp
  Hex_Digit_Display hex_digit_display_10 (.value(multiplexer_1_out[7:4]));  // open: dp
  Hex_Digit_Display hex_digit_display_11 (.value(multiplexer_2_out));  // open: dp
  Hex_Digit_Display hex_digit_display_12 (.value(multiplexer_2_out_2));  // open: dp
  MEM mem_1 (
    .Address(demultiplexer_1_out1), .DataIn(regs_1_data2), .DataOut(mem_1_dataout), .sw(sw), .clk(clk),
    .lw(lw));  // open: clr

  // Other names for the same wires on the sheet: _0 = in_1
endmodule

// Ctrl Logic
module Control_Logic (
  input  [3:0] op,
  output j,
  output b,
  output ldMem,
  output strMem,
  output strReg
);

  wire and_3_out, and_4_out, and_6_out, and_7_out, and_8_out, and_9_out, not_1_out, not_2_out, not_3_out,
       not_4_out, not_5_out, not_6_out, not_7_out, not_8_out, not_9_out;

  not not_1 (not_1_out, op[2]);
  not not_2 (not_2_out, op[1]);
  not not_3 (not_3_out, op[2]);
  not not_4 (not_4_out, op[0]);
  not not_5 (not_5_out, op[2]);
  not not_6 (not_6_out, op[1]);
  and and_1 (ldMem, op[3], op[1], op[0]);
  and and_2 (strMem, op[3], op[2]);
  not not_7 (not_7_out, op[3]);
  not not_8 (not_8_out, op[3]);
  not not_9 (not_9_out, op[3]);
  and and_3 (and_3_out, op[3], not_1_out, not_2_out);
  and and_4 (and_4_out, op[3], not_3_out, not_4_out);
  and and_5 (b, op[3], not_5_out, not_6_out);
  and and_6 (and_6_out, not_7_out, op[0]);
  and and_7 (and_7_out, not_8_out, op[1]);
  and and_8 (and_8_out, op[1], op[0]);
  and and_9 (and_9_out, not_9_out, op[2]);
  or or_1 (j, and_3_out, and_4_out);
  or or_2 (strReg, and_6_out, and_7_out, and_8_out, and_9_out);
endmodule

module ALU (
  input  [15:0] data1,
  input  [15:0] data2,
  input  [15:0] immed,
  output [15:0] out,
  output zero
);

  wire and_2_out, and_3_out, and_6_out, bne, isImmed, isRight, offset_01;
  wire [0:0] slt;
  wire [15:0] multiplexer_1_out, multiplexer_2_out, multiplexer_4_out, negator_1_out, \or , shift, sub, sum;

  and and_1 (offset_01, immed[15], immed[14], ~immed[13], ~immed[12]);  // AND_Gate
  and and_2 (and_2_out, immed[15], ~immed[14], immed[13], immed[12]);  // AND_Gate
  and and_3 (and_3_out, ~immed[15], ~immed[14], immed[13], immed[12]);  // AND_Gate
  and and_4 (isRight, ~immed[12], immed[13], immed[14], ~immed[15]);  // AND_Gate
  and and_5 (bne, immed[12], ~immed[13], ~immed[14], immed[15]);  // AND_Gate
  or or_1 (isImmed, offset_01, and_2_out, and_3_out);
  Multiplexer #(.width(16)) multiplexer_1 (
    .in0({{12{1'b0}}, immed[3:0]}), .in1({{12{1'b0}}, immed[11:8]}), .out(multiplexer_1_out), .sel(offset_01));  // open: en
  Adder #(.width(16)) adder_1 (.a(data1), .b(multiplexer_2_out), .out(sum));  // open: cin, cout
  Multiplexer #(.width(16)) multiplexer_2 (
    .in0(data2), .in1(multiplexer_1_out), .out(multiplexer_2_out), .sel(isImmed));  // open: en
  Subtractor #(.width(16)) subtractor_1 (.a(data1), .b(multiplexer_2_out), .out(sub));  // open: bin, bout
  Comparator #(.width(16)) comparator_1 (.a(data1), .b(multiplexer_2_out), .lt(slt[0]));  // open: gt, eq
  Multiplexer #(.select(4), .width(16)) multiplexer_3 (
    .in0({16{1'b0}}), .in1({{8{1'b0}}, immed[7:0]}), .in2(sum), .in3(sum), .in4(\or ), .in5(shift),
    .in6(shift), .in7({{15{1'b0}}, slt[0]}), .in8(sub), .in9(sub), .in10({4'b0000, immed[11:0]}), .in11(sum),
    .in12(sum), .out(out), .sel(immed[15:12]));  // open: in13, in14, in15, en
  Multiplexer #(.width(16)) multiplexer_4 (
    .in0(multiplexer_2_out), .in1(negator_1_out), .out(multiplexer_4_out), .sel(isRight));  // open: en
  Negator #(.width(16)) negator_1 (.in(multiplexer_2_out), .out(negator_1_out));
  assign \or  = data1 | multiplexer_2_out;  // OR_Gate or_2, 16 bits wide
  and and_6 (and_6_out, ~out[0], ~out[1], ~out[2], ~out[3], ~out[4], ~out[5], ~out[6], ~out[7], ~out[8], ~out[9], ~out[10], ~out[11], ~out[12], ~out[13], ~out[14], ~out[15]);  // AND_Gate
  Shifter #(.width(16)) shifter_1 (.in(data1), .\dist (multiplexer_4_out[3:0]), .out(shift));
  xor xor_1 (zero, and_6_out, bne);

  // Other names for the same wires on the sheet: op[3:0] = immed[15:12]; immed_0_3[3:0] = immed[3:0];
  //   immed_0_7[7:0] = immed[7:0]; immed_0_11[11:0] = immed[11:0]; immed_8_11[3:0] = immed[11:8]
endmodule

module Regs (
  input  [3:0] rs,
  input  str,
  input  [3:0] rd,
  input  [3:0] rt,
  input  [15:0] in,
  input  clk,
  input  clr,
  output [15:0] data1,
  output [15:0] data2,
  output [15:0] jumper
);

  wire demultiplexer_1_out1, demultiplexer_1_out2, demultiplexer_1_out3, demultiplexer_1_out4,
       demultiplexer_1_out5, demultiplexer_1_out6, demultiplexer_1_out7, demultiplexer_1_out8,
       demultiplexer_1_out9, demultiplexer_1_out10, demultiplexer_1_out11, demultiplexer_1_out12,
       demultiplexer_1_out13, demultiplexer_1_out14, demultiplexer_1_out15;
  wire [15:0] demultiplexer_2_out0, demultiplexer_2_out1, demultiplexer_2_out2, demultiplexer_2_out3,
       demultiplexer_2_out4, demultiplexer_2_out5, demultiplexer_2_out6, demultiplexer_2_out7,
       demultiplexer_2_out8, demultiplexer_2_out9, demultiplexer_2_out10, demultiplexer_2_out11,
       demultiplexer_2_out12, demultiplexer_2_out13, demultiplexer_2_out14, demultiplexer_2_out15,
       register_1_q, register_2_q, register_3_q, register_4_q, register_5_q, register_6_q, register_7_q,
       register_8_q, register_9_q, register_10_q, register_11_q, register_12_q, register_13_q, register_14_q,
       register_15_q;

  Demultiplexer #(.select(4)) demultiplexer_1 (
    .out1(demultiplexer_1_out1), .out2(demultiplexer_1_out2), .out3(demultiplexer_1_out3),
    .out4(demultiplexer_1_out4), .out5(demultiplexer_1_out5), .out6(demultiplexer_1_out6),
    .out7(demultiplexer_1_out7), .out8(demultiplexer_1_out8), .out9(demultiplexer_1_out9),
    .out10(demultiplexer_1_out10), .out11(demultiplexer_1_out11), .out12(demultiplexer_1_out12),
    .out13(demultiplexer_1_out13), .out14(demultiplexer_1_out14), .out15(demultiplexer_1_out15), .in(str),
    .sel(rd));  // open: out0, en
  Demultiplexer #(.select(4), .width(16)) demultiplexer_2 (
    .out0(demultiplexer_2_out0), .out1(demultiplexer_2_out1), .out2(demultiplexer_2_out2),
    .out3(demultiplexer_2_out3), .out4(demultiplexer_2_out4), .out5(demultiplexer_2_out5),
    .out6(demultiplexer_2_out6), .out7(demultiplexer_2_out7), .out8(demultiplexer_2_out8),
    .out9(demultiplexer_2_out9), .out10(demultiplexer_2_out10), .out11(demultiplexer_2_out11),
    .out12(demultiplexer_2_out12), .out13(demultiplexer_2_out13), .out14(demultiplexer_2_out14),
    .out15(demultiplexer_2_out15), .in(in), .sel(rd));  // open: en
  Register #(.width(16)) register_1 (.D(demultiplexer_2_out0), .en(1'b0), .Q(register_1_q), .clk(clk), .clr(clr));
  Register #(.width(16)) register_2 (
    .D(demultiplexer_2_out1), .en(demultiplexer_1_out1), .Q(register_2_q), .clk(clk), .clr(clr));
  Register #(.width(16)) register_3 (
    .D(demultiplexer_2_out2), .en(demultiplexer_1_out2), .Q(register_3_q), .clk(clk), .clr(clr));
  Register #(.width(16)) register_4 (
    .D(demultiplexer_2_out3), .en(demultiplexer_1_out3), .Q(register_4_q), .clk(clk), .clr(clr));
  Register #(.width(16)) register_5 (
    .D(demultiplexer_2_out4), .en(demultiplexer_1_out4), .Q(register_5_q), .clk(clk), .clr(clr));
  Register #(.width(16)) register_6 (
    .D(demultiplexer_2_out5), .en(demultiplexer_1_out5), .Q(register_6_q), .clk(clk), .clr(clr));
  Register #(.width(16)) register_7 (
    .D(demultiplexer_2_out6), .en(demultiplexer_1_out6), .Q(register_7_q), .clk(clk), .clr(clr));
  Register #(.width(16)) register_8 (
    .D(demultiplexer_2_out7), .en(demultiplexer_1_out7), .Q(register_8_q), .clk(clk), .clr(clr));
  Register #(.width(16)) register_9 (
    .D(demultiplexer_2_out8), .en(demultiplexer_1_out8), .Q(register_9_q), .clk(clk), .clr(clr));
  Register #(.width(16)) register_10 (
    .D(demultiplexer_2_out9), .en(demultiplexer_1_out9), .Q(register_10_q), .clk(clk), .clr(clr));
  Register #(.width(16)) register_11 (
    .D(demultiplexer_2_out10), .en(demultiplexer_1_out10), .Q(register_11_q), .clk(clk), .clr(clr));
  Register #(.width(16)) register_12 (
    .D(demultiplexer_2_out11), .en(demultiplexer_1_out11), .Q(register_12_q), .clk(clk), .clr(clr));
  Register #(.width(16)) register_13 (
    .D(demultiplexer_2_out12), .en(demultiplexer_1_out12), .Q(register_13_q), .clk(clk), .clr(clr));
  Register #(.width(16)) register_14 (
    .D(demultiplexer_2_out13), .en(demultiplexer_1_out13), .Q(register_14_q), .clk(clk), .clr(clr));
  Register #(.width(16)) register_15 (
    .D(demultiplexer_2_out14), .en(demultiplexer_1_out14), .Q(register_15_q), .clk(clk), .clr(clr));
  Register #(.width(16)) register_16 (
    .D(demultiplexer_2_out15), .en(demultiplexer_1_out15), .Q(jumper), .clk(clk), .clr(clr));
  Multiplexer #(.select(4), .width(16)) multiplexer_1 (
    .in0(register_1_q), .in1(register_2_q), .in2(register_3_q), .in3(register_4_q), .in4(register_5_q),
    .in5(register_6_q), .in6(register_7_q), .in7(register_8_q), .in8(register_9_q), .in9(register_10_q),
    .in10(register_11_q), .in11(register_12_q), .in12(register_13_q), .in13(register_14_q),
    .in14(register_15_q), .in15(jumper), .out(data1), .sel(rs));  // open: en
  Multiplexer #(.select(4), .width(16)) multiplexer_2 (
    .in0(register_1_q), .in1(register_2_q), .in2(register_3_q), .in3(register_4_q), .in4(register_5_q),
    .in5(register_6_q), .in6(register_7_q), .in7(register_8_q), .in8(register_9_q), .in9(register_10_q),
    .in10(register_11_q), .in11(register_12_q), .in12(register_13_q), .in13(register_14_q),
    .in14(register_15_q), .in15(jumper), .out(data2), .sel(rt));  // open: en
endmodule

module ROM (
  input  [15:0] Address,
  input  gt,
  input  clk,
  input  clr,
  output [15:0] Instruction
);

  wire adder_1_cout, or_1_out;
  wire [15:0] adder_1_out, multiplexer_1_out, PC_q;

  Multiplexer #(.width(16)) multiplexer_1 (
    .in0(adder_1_out), .in1(Address), .out(multiplexer_1_out), .sel(gt));  // open: en
  Register #(.width(16)) PC (.D(multiplexer_1_out), .Q(PC_q), .clk(clk), .clr(or_1_out));  // open: en
  or or_1 (or_1_out, adder_1_cout, clr);
  Adder #(.width(16)) adder_1 (.a(16'h1), .b(PC_q), .out(adder_1_out), .cout(adder_1_cout));  // open: cin
  ROM_part #(.addrWidth(16), .dataWidth(16)) rom_1 (.addr(PC_q), .data(Instruction));  // open: sel

  // Notes on the sheet:
  //   contents of rom_1 (hex, n*v repeats v):
  //   b100 1201 b320 1f0e 8021 3221 b420 7534 1f0b 8050 2340 a003 c023 a00d
endmodule

module MEM (
  input  [15:0] Address,
  input  sw,
  input  clk,
  input  lw,
  input  clr,
  input  [15:0] DataIn,
  output [15:0] DataOut
);

  RAM #(.addrWidth(16), .dataWidth(16), .bus("separate")) ram_1 (
    .addr(Address), .din(DataIn), .data(DataOut), .str(sw), .sel(1'b1), .clk(clk), .ld(lw), .clr(clr));
endmodule

// b
module branch (
  input  b,
  input  j,
  input  z,
  output j_2
);

  wire and_1_out, and_2_out;

  and and_1 (and_1_out, ~b, j);  // AND_Gate
  or or_1 (j_2, and_1_out, and_2_out);
  and and_2 (and_2_out, j, z);
endmodule
