// Logisim project sketch.circ as structural Verilog: 7 circuits, main circuit CPU Logic
module main (
);

  wire button_out, clk, clock_1_out, clr, lw, on, sw;
  wire [7:0] cpu_logic_1_ram_address, cpu_logic_1_ram_dbus, ram_1_data;

  Clock clock_1 (.out(clock_1_out));
  switch switch_1 (.in_1(button_out), .out_2(on));
  Button button (.out(button_out));
  Button u_clr (.out(clr));
  assign clk = on ? clock_1_out : 1'bz;  // Controlled_Buffer controlled_buffer_1
  CPU_Logic cpu_logic_1 (
    .clr(clr), .clk(clk), .Data_In(ram_1_data), .RAM_dbus(cpu_logic_1_ram_dbus),
    .RAM_Address(cpu_logic_1_ram_address));  // open: lw, sw
  RAM #(.bus("separate")) ram_1 (
    .addr(cpu_logic_1_ram_dbus), .din(cpu_logic_1_ram_address), .data(ram_1_data), .str(sw), .sel(on),
    .clk(clk), .ld(lw), .clr(clr));
endmodule

// CPU
module CPU_Logic (
  input  clr,
  input  [7:0] Data_In,
  input  clk,
  output [7:0] RAM_dbus,
  output [7:0] RAM_Address,
  output lw,
  output sw
);

  wire control_1_str_reg;
  wire [2:0] control_1_alu_op;
  wire [7:0] pc_1_i, undriven;

  PC pc_1 (.jump_address(undriven), .I(pc_1_i));  // open: jump_branch, clk, reset
  Control control_1 (
    .Instruction(pc_1_i), .lw(lw), .sw(sw), .str_reg(control_1_str_reg), .ALU_op(control_1_alu_op));  // open: ld_immed, jump, ld_reg
  // Regs regs_1: pin names not known; wires that end beside it: control_1_str_reg, clk, clr
  ALU alu_1 ();  // open: Data1, Data2, ALU_op, DataOut, zero
endmodule

module PC (
  input  [7:0] jump_address,
  input  jump_branch,
  input  clk,
  input  reset,
  output [7:0] I
);

  wire [7:0] adder_1_out, multiplexer_1_out, register_1_q;

  Multiplexer #(.width(8)) multiplexer_1 (
    .in0(adder_1_out), .in1(jump_address), .out(multiplexer_1_out), .sel(jump_branch));  // open: en
  Register register_1 (.D(multiplexer_1_out), .Q(register_1_q), .clk(clk), .clr(reset));  // open: en
  Adder adder_1 (.a(8'h8), .b(register_1_q), .out(adder_1_out));  // open: cin, cout
  ROM rom_1 (.addr(register_1_q), .data(I), .sel(1'b1));

  // Notes on the sheet:
  //   contents of rom_1 (hex, n*v repeats v):
  //   aa ff
endmodule

module Control (
  input  [7:0] Instruction,
  output lw,
  output sw,
  output ld_immed,
  output jump,
  output str_reg,
  output ld_reg,
  output [2:0] ALU_op
);


  // Other names for the same wires on the sheet: Op[3:0] = Instruction[3:0]
endmodule

module Regs (
  input  str,
  input  [2:0] RegSelect,
  input  [2:0] RegTelect,
  input  [2:0] RedDest,
  input  [7:0] DataIn,
  input  clk,
  input  clr,
  output [7:0] Data1,
  output [7:0] Data2
);

  wire demultiplexer_1_out0, demultiplexer_1_out1, demultiplexer_1_out2, demultiplexer_1_out3,
       demultiplexer_1_out4, demultiplexer_1_out5, demultiplexer_1_out6, demultiplexer_1_out7;
  wire [7:0] demultiplexer_2_out0, demultiplexer_2_out1, demultiplexer_2_out2, demultiplexer_2_out3,
       demultiplexer_2_out4, demultiplexer_2_out5, demultiplexer_2_out6, demultiplexer_2_out7, register_1_q,
       register_2_q, register_3_q, register_4_q, register_5_q, register_6_q, register_7_q, register_8_q;

  Demultiplexer #(.select(3)) demultiplexer_1 (
    .out0(demultiplexer_1_out0), .out1(demultiplexer_1_out1), .out2(demultiplexer_1_out2),
    .out3(demultiplexer_1_out3), .out4(demultiplexer_1_out4), .out5(demultiplexer_1_out5),
    .out6(demultiplexer_1_out6), .out7(demultiplexer_1_out7), .in(str), .sel(RedDest));  // open: en
  Demultiplexer #(.select(3), .width(8)) demultiplexer_2 (
    .out0(demultiplexer_2_out0), .out1(demultiplexer_2_out1), .out2(demultiplexer_2_out2),
    .out3(demultiplexer_2_out3), .out4(demultiplexer_2_out4), .out5(demultiplexer_2_out5),
    .out6(demultiplexer_2_out6), .out7(demultiplexer_2_out7), .in(DataIn), .sel(RedDest));  // open: en
  Register register_1 (.D(demultiplexer_2_out0), .en(demultiplexer_1_out0), .Q(register_1_q), .clk(clk), .clr(clr));
  Register register_2 (.D(demultiplexer_2_out1), .en(demultiplexer_1_out1), .Q(register_2_q), .clk(clk), .clr(clr));
  Register register_3 (.D(demultiplexer_2_out2), .en(demultiplexer_1_out2), .Q(register_3_q), .clk(clk), .clr(clr));
  Register register_4 (.D(demultiplexer_2_out3), .en(demultiplexer_1_out3), .Q(register_4_q), .clk(clk), .clr(clr));
  Register register_5 (.D(demultiplexer_2_out4), .en(demultiplexer_1_out4), .Q(register_5_q), .clk(clk), .clr(clr));
  Register register_6 (.D(demultiplexer_2_out5), .en(demultiplexer_1_out5), .Q(register_6_q), .clk(clk), .clr(clr));
  Register register_7 (.D(demultiplexer_2_out6), .en(demultiplexer_1_out6), .Q(register_7_q), .clk(clk), .clr(clr));
  Register register_8 (.D(demultiplexer_2_out7), .en(demultiplexer_1_out7), .Q(register_8_q), .clk(clk), .clr(clr));
  Multiplexer #(.select(3), .width(8)) multiplexer_1 (
    .in0(register_1_q), .in1(register_2_q), .in2(register_3_q), .in3(register_4_q), .in4(register_5_q),
    .in5(register_6_q), .in6(register_7_q), .in7(register_8_q), .out(Data1), .sel(RegSelect));  // open: en
  Multiplexer #(.select(3), .width(8)) multiplexer_2 (
    .in0(register_1_q), .in1(register_2_q), .in2(register_3_q), .in3(register_4_q), .in4(register_5_q),
    .in5(register_6_q), .in6(register_7_q), .in7(register_8_q), .out(Data2), .sel(RegTelect));  // open: en

  // Other names for the same wires on the sheet: RS[2:0] = RegSelect; RT[2:0] = RegTelect
endmodule

module ALU (
  input  [7:0] Data1,
  input  [7:0] Data2,
  input  [2:0] ALU_op,
  output [7:0] DataOut,
  output zero
);

  wire comparator_1_gt;
  wire [2:0] bit_extender_1_out, bit_extender_2_out;
  wire [7:0] adder_1_out, bit_extender_3_out, divider_1_out, multiplier_1_out, not_1_out, shifter_1_out,
       shifter_2_out, subtractor_1_out, undriven;

  Bit_Extender #(.out_width(3)) bit_extender_1 (.in(Data2), .out(bit_extender_1_out));
  Bit_Extender #(.out_width(3)) bit_extender_2 (.in(Data2), .out(bit_extender_2_out));
  Adder adder_1 (.a(Data1), .b(Data2), .out(adder_1_out));  // open: cin, cout
  Subtractor subtractor_1 (.a(Data1), .b(Data2), .out(subtractor_1_out));  // open: bin, bout
  Multiplier multiplier_1 (.a(Data1), .b(Data2), .out(multiplier_1_out));  // open: cin, cout
  Divider divider_1 (.a(Data1), .b(Data2), .out(divider_1_out));  // open: upper, rem
  Shifter #(.shift("lr")) shifter_1 (.in(Data1), .\dist (bit_extender_1_out), .out(shifter_1_out));
  Shifter shifter_2 (.in(Data1), .\dist (bit_extender_2_out), .out(shifter_2_out));
  assign bit_extender_3_out = {{7{1'b0}}, comparator_1_gt};  // Bit_Extender bit_extender_3
  Comparator comparator_1 (.a(Data1), .b(Data2), .gt(comparator_1_gt));  // open: eq, lt
  Multiplexer #(.select(3), .width(8)) multiplexer_1 (
    .in0(adder_1_out), .in1(subtractor_1_out), .in2(multiplier_1_out), .in3(divider_1_out),
    .in4(shifter_1_out), .in5(shifter_2_out), .in6(undriven), .in7(bit_extender_3_out), .out(DataOut),
    .sel(ALU_op));  // open: en
  assign not_1_out = ~DataOut;  // NOT_Gate not_1, 8 bits wide
  and and_1 (zero, not_1_out[0], not_1_out[1], not_1_out[2], not_1_out[3], not_1_out[4], not_1_out[5], not_1_out[6], not_1_out[7]);
endmodule

module switch (
  input  in_1,
  output out_2
);

  wire d_ff_1_qn;

  D_Flip_Flop d_ff_1 (.clk(in_1), .D(d_ff_1_qn), .Q(out_2), .Qn(d_ff_1_qn));  // open: preset, en, reset
endmodule
