// Logisim project sketch_16x.circ as structural Verilog: 7 circuits, main circuit CPU
module CPU (
  input  in_1,
  input  [15:0] in_2,
  output [15:0] out_3,
  output [15:0] out_4,
  output [15:0] out_5
);

  wire alu_1_p5, b, clk, control_logic_1_jump, control_logic_1_strreg, controlled_buffer_1_out, j, ldMem,
       not_1_out, strMem;
  wire [2:0] control_logic_1_aluop;
  wire [15:0] A, adder_1_out, D2, demultiplexer_1_out0, demultiplexer_1_out1, multiplexer_1_out,
       multiplexer_4_out, PC_q, ram_1_dataout, regs_1_data1, undriven;

  Clock clock_1 (.out(clk));
  Control_Logic_2 control_logic_1 (
    .OP(out_3[15:12]), .ldMem(ldMem), .strMem(strMem), .strReg(control_logic_1_strreg), .branch(b),
    .jump(control_logic_1_jump), .ALUOP(control_logic_1_aluop));
  Register #(.width(16)) PC (.D(multiplexer_1_out), .Q(PC_q), .clk(clk), .clr(in_1));  // open: en
  Multiplexer #(.width(16)) multiplexer_1 (.in0(adder_1_out), .in1(A), .out(multiplexer_1_out), .sel(j));  // open: en
  Regs regs_1 (
    .RegSelect(out_3[7:4]), .RegTelect(out_3[3:0]), .RedDest(out_3[11:8]), .DataIn(multiplexer_4_out),
    .Data1(regs_1_data1), .Data2(D2), .str(control_logic_1_strreg), .clk(clk), .clr(in_1));
  Adder #(.width(16)) adder_1 (.a(16'h1), .b(PC_q), .out(adder_1_out));  // open: cin, cout
  ROM_part #(.addrWidth(16), .dataWidth(16)) rom_1 (.addr(PC_q), .data(out_3));  // open: sel
  assign controlled_buffer_1_out = not_1_out ? control_logic_1_jump : 1'bz;  // Controlled_Buffer controlled_buffer_1
  not not_1 (not_1_out, alu_1_p5);
  // ALU alu_1: pin names not known; wires that end beside it: regs_1_data1, D2, A, control_logic_1_aluop, alu_1_p5, out_5
  Multiplexer #(.width(16)) multiplexer_2 (.in1(undriven), .out(A), .sel(b));  // open: in0, en
  Multiplexer multiplexer_3 (.in0(control_logic_1_jump), .in1(controlled_buffer_1_out), .out(j), .sel(b));  // open: en
  Demultiplexer #(.width(16)) demultiplexer_1 (
    .out0(demultiplexer_1_out0), .out1(demultiplexer_1_out1), .in(out_5), .sel(ldMem));  // open: en
  Multiplexer #(.width(16)) multiplexer_4 (
    .in0(demultiplexer_1_out0), .in1(ram_1_dataout), .out(multiplexer_4_out), .sel(ldMem));  // open: en
  RAM ram_1 (
    .Address(demultiplexer_1_out1), .DataIn(D2), .DataOut(ram_1_dataout), .sw(strMem), .clk(clk), .lw(ldMem),
    .clr(in_1));
  Control_Logic control_logic_2 ();  // open: ldMem, strMem, strReg, branch, jump

  // Other names for the same wires on the sheet: I[15:0] = out_3; clr = in_1

  // Notes on the sheet:
  //   Data1
  //   Data2
  //   Immed
  //   contents of rom_1 (hex, n*v repeats v):
  //   110a 0 d000
endmodule

// Ctrl
module Control_Logic (
  output ldMem,
  output strMem,
  output strReg,
  output branch,
  output jump
);

  wire and_1_out, and_2_out, and_5_out, and_6_out, and_7_out, and_8_out, and_9_out, and_10_out, and_11_out,
       and_12_out, and_13_out, and_14_out, and_15_out, and_16_out, and_17_out, and_18_out, not_1_out,
       not_2_out, not_3_out, not_4_out, not_5_out, not_6_out, not_7_out, not_8_out, not_9_out, not_10_out,
       not_11_out, not_12_out, not_13_out, not_14_out, not_15_out, not_16_out, not_17_out, not_18_out,
       not_19_out, not_20_out, undriven, undriven_2, undriven_3, undriven_4;
  wire [2:0] or_4_out;

  not not_1 (not_1_out, undriven_2);
  not not_2 (not_2_out, undriven_3);
  not not_3 (not_3_out, undriven_4);
  not not_4 (not_4_out, undriven);
  not not_5 (not_5_out, undriven);
  not not_6 (not_6_out, undriven);
  not not_7 (not_7_out, undriven_2);
  not not_8 (not_8_out, undriven_3);
  not not_9 (not_9_out, undriven_2);
  not not_10 (not_10_out, undriven_3);
  not not_11 (not_11_out, undriven_4);
  and and_1 (and_1_out, undriven, undriven_3, undriven_4);
  and and_2 (and_2_out, undriven, undriven_2);
  not not_12 (not_12_out, undriven_2);
  not not_13 (not_13_out, undriven_3);
  not not_14 (not_14_out, undriven_4);
  not not_15 (not_15_out, undriven_3);
  not not_16 (not_16_out, undriven_4);
  not not_17 (not_17_out, undriven);
  not not_18 (not_18_out, undriven_4);
  not not_19 (not_19_out, undriven_3);
  not not_20 (not_20_out, undriven_4);
  and and_3 (ldMem, undriven, not_1_out, not_2_out, undriven_4);
  and and_4 (strMem, undriven, undriven_3, not_3_out);
  and and_5 (and_5_out, not_4_out, undriven_4);
  and and_6 (and_6_out, not_5_out, undriven_3);
  and and_7 (and_7_out, not_6_out, undriven_2);
  and and_8 (and_8_out, undriven, not_7_out, not_8_out);
  and and_9 (and_9_out, undriven, not_9_out, undriven_3, undriven_4);
  and and_10 (and_10_out, undriven, undriven_2, not_10_out, not_11_out);
  or or_1 (jump, and_1_out, and_2_out);
  and and_11 (and_11_out, not_12_out, not_13_out, not_14_out);
  and and_12 (and_12_out, undriven_2, undriven_4);
  and and_13 (and_13_out, undriven_2, undriven_3);
  and and_14 (and_14_out, not_15_out, not_16_out);
  and and_15 (and_15_out, undriven_3, undriven_4);
  and and_16 (and_16_out, not_17_out, not_18_out);
  and and_17 (and_17_out, not_19_out, not_20_out);
  and and_18 (and_18_out, undriven, undriven_3, undriven_4);
  or or_2 (strReg, and_5_out, and_6_out, and_7_out, and_8_out);
  or or_3 (branch, and_9_out, and_10_out);
  or or_4 (or_4_out[0], and_11_out, and_12_out, and_13_out);
  or or_5 (or_4_out[1], and_14_out, and_15_out, undriven);
  or or_6 (or_4_out[2], and_16_out, and_17_out, and_18_out);
endmodule

module ALU (
  input  [3:0] ALUOp,
  input  [15:0] Data1,
  input  [15:0] Data2,
  input  [15:0] Immed,
  input  in_5,
  output [15:0] DataOut,
  output Zero
);

  wire and_1_out, comparator_1_gt, controlled_inverter_1_out;
  wire [3:0] bitselector_1_out;
  wire [15:0] adder_1_out, adder_2_out, bit_extender_1_out, shifter_1_out, shifter_2_out, shifter_3_out,
       subtractor_1_out, subtractor_2_out, undriven, undriven_2;

  Adder #(.width(16)) adder_1 (.a(Data1), .b(Data2), .out(adder_1_out));  // open: cin, cout
  Adder #(.width(16)) adder_2 (.a(Data1), .b(Immed), .out(adder_2_out));  // open: cin, cout
  Subtractor #(.width(16)) subtractor_1 (.a(Data1), .b(Data2), .out(subtractor_1_out));  // open: bin, bout
  Subtractor #(.width(16)) subtractor_2 (.a(Data1), .b(Immed), .out(subtractor_2_out));  // open: bin, bout
  Shifter #(.width(16)) shifter_1 (.in(Data1), .\dist (Immed[15:12]), .out(shifter_1_out));
  Shifter #(.width(16), .shift("lr")) shifter_2 (.in(Data1), .\dist (Immed[15:12]), .out(shifter_2_out));
  Comparator #(.width(16)) comparator_1 (.a(Data1), .b(Data2), .gt(comparator_1_gt));  // open: eq, lt
  BitSelector #(.width(16), .group(4)) bitselector_1 (.in(Immed), .out(bitselector_1_out), .sel(2'b10));
  assign bit_extender_1_out = {{15{1'b0}}, comparator_1_gt};  // Bit_Extender bit_extender_1
  Shifter #(.width(16), .shift("lr")) shifter_3 (
    .in({4'b0000, bitselector_1_out, {8{1'b0}}}), .\dist (4'b1000), .out(shifter_3_out));
  Multiplexer #(.select(4), .width(16)) multiplexer_1 (
    .in0(Immed), .in1(adder_1_out), .in2(adder_2_out), .in3(subtractor_1_out), .in4(subtractor_2_out),
    .in5(shifter_1_out), .in6(shifter_2_out), .in7(bit_extender_1_out), .in8(shifter_3_out),
    .in9(undriven_2), .in10(undriven), .sel(ALUOp));  // open: in11, in12, in13, in14, in15, out, en
  and and_1 (and_1_out, DataOut[0], DataOut[1], DataOut[2], DataOut[3], DataOut[4], DataOut[5], DataOut[6], DataOut[7], DataOut[8], DataOut[9], DataOut[10], DataOut[11], DataOut[12], DataOut[13], DataOut[14], DataOut[15]);
  Multiplexer multiplexer_2 (.in0(and_1_out), .in1(controlled_inverter_1_out), .out(Zero));  // open: sel, en
  assign controlled_inverter_1_out = in_5 ? ~and_1_out : 1'bz;  // Controlled_Inverter controlled_inverter_1
endmodule

module Regs (
  input  str,
  input  [3:0] RegSelect,
  input  [3:0] RegTelect,
  input  [3:0] RedDest,
  input  [15:0] DataIn,
  input  clk,
  input  clr,
  output [15:0] Data1,
  output [15:0] Data2
);

  wire demultiplexer_1_out1, demultiplexer_1_out2, demultiplexer_1_out3, demultiplexer_1_out4,
       demultiplexer_1_out5, demultiplexer_1_out6, demultiplexer_1_out7, demultiplexer_1_out8,
       demultiplexer_1_out9, demultiplexer_1_out10, demultiplexer_1_out11, demultiplexer_1_out12,
       demultiplexer_1_out13, demultiplexer_1_out14, demultiplexer_1_out15;
  wire [15:0] demultiplexer_2_out0, demultiplexer_2_out1, demultiplexer_2_out2, demultiplexer_2_out3,
       demultiplexer_2_out4, demultiplexer_2_out5, demultiplexer_2_out6, demultiplexer_2_out7,
       demultiplexer_2_out8, demultiplexer_2_out9, demultiplexer_2_out10, demultiplexer_2_out11,
       demultiplexer_2_out12, demultiplexer_2_out13, demultiplexer_2_out14, demultiplexer_2_out15,
       register_1_q, register_2_q, register_3_q, register_4_q, register_5_q, register_6_q, register_7_q,
       register_8_q, register_9_q, register_10_q, register_11_q, register_12_q, register_13_q, register_14_q,
       register_15_q, register_16_q;

  Demultiplexer #(.select(4)) demultiplexer_1 (
    .out1(demultiplexer_1_out1), .out2(demultiplexer_1_out2), .out3(demultiplexer_1_out3),
    .out4(demultiplexer_1_out4), .out5(demultiplexer_1_out5), .out6(demultiplexer_1_out6),
    .out7(demultiplexer_1_out7), .out8(demultiplexer_1_out8), .out9(demultiplexer_1_out9),
    .out10(demultiplexer_1_out10), .out11(demultiplexer_1_out11), .out12(demultiplexer_1_out12),
    .out13(demultiplexer_1_out13), .out14(demultiplexer_1_out14), .out15(demultiplexer_1_out15), .in(str),
    .sel(RedDest));  // open: out0, en
  Demultiplexer #(.select(4), .width(16)) demultiplexer_2 (
    .out0(demultiplexer_2_out0), .out1(demultiplexer_2_out1), .out2(demultiplexer_2_out2),
    .out3(demultiplexer_2_out3), .out4(demultiplexer_2_out4), .out5(demultiplexer_2_out5),
    .out6(demultiplexer_2_out6), .out7(demultiplexer_2_out7), .out8(demultiplexer_2_out8),
    .out9(demultiplexer_2_out9), .out10(demultiplexer_2_out10), .out11(demultiplexer_2_out11),
    .out12(demultiplexer_2_out12), .out13(demultiplexer_2_out13), .out14(demultiplexer_2_out14),
    .out15(demultiplexer_2_out15), .in(DataIn), .sel(RedDest));  // open: en
  Register #(.width(16)) register_1 (.D(demultiplexer_2_out0), .en(1'b0), .Q(register_1_q), .clk(clk), .clr(clr));
  Register #(.width(16)) register_2 (
    .D(demultiplexer_2_out1), .en(demultiplexer_1_out1), .Q(register_2_q), .clk(clk), .clr(clr));
  Register #(.width(16)) register_3 (
    .D(demultiplexer_2_out2), .en(demultiplexer_1_out2), .Q(register_3_q), .clk(clk), .clr(clr));
  Register #(.width(16)) register_4 (
    .D(demultiplexer_2_out3), .en(demultiplexer_1_out3), .Q(register_4_q), .clk(clk), .clr(clr));
  Register #(.width(16)) register_5 (
    .D(demultiplexer_2_out4), .en(demultiplexer_1_out4), .Q(register_5_q), .clk(clk), .clr(clr));
  Register #(.width(16)) register_6 (
    .D(demultiplexer_2_out5), .en(demultiplexer_1_out5), .Q(register_6_q), .clk(clk), .clr(clr));
  Register #(.width(16)) register_7 (
    .D(demultiplexer_2_out6), .en(demultiplexer_1_out6), .Q(register_7_q), .clk(clk), .clr(clr));
  Register #(.width(16)) register_8 (
    .D(demultiplexer_2_out7), .en(demultiplexer_1_out7), .Q(register_8_q), .clk(clk), .clr(clr));
  Register #(.width(16)) register_9 (
    .D(demultiplexer_2_out8), .en(demultiplexer_1_out8), .Q(register_9_q), .clk(clk), .clr(clr));
  Register #(.width(16)) register_10 (
    .D(demultiplexer_2_out9), .en(demultiplexer_1_out9), .Q(register_10_q), .clk(clk), .clr(clr));
  Register #(.width(16)) register_11 (
    .D(demultiplexer_2_out10), .en(demultiplexer_1_out10), .Q(register_11_q), .clk(clk), .clr(clr));
  Register #(.width(16)) register_12 (
    .D(demultiplexer_2_out11), .en(demultiplexer_1_out11), .Q(register_12_q), .clk(clk), .clr(clr));
  Register #(.width(16)) register_13 (
    .D(demultiplexer_2_out12), .en(demultiplexer_1_out12), .Q(register_13_q), .clk(clk), .clr(clr));
  Register #(.width(16)) register_14 (
    .D(demultiplexer_2_out13), .en(demultiplexer_1_out13), .Q(register_14_q), .clk(clk), .clr(clr));
  Register #(.width(16)) register_15 (
    .D(demultiplexer_2_out14), .en(demultiplexer_1_out14), .Q(register_15_q), .clk(clk), .clr(clr));
  Register #(.width(16)) register_16 (
    .D(demultiplexer_2_out15), .en(demultiplexer_1_out15), .Q(register_16_q), .clk(clk), .clr(clr));
  Multiplexer #(.select(4), .width(16)) multiplexer_1 (
    .in0(register_1_q), .in1(register_2_q), .in2(register_3_q), .in3(register_4_q), .in4(register_5_q),
    .in5(register_6_q), .in6(register_7_q), .in7(register_8_q), .in8(register_9_q), .in9(register_10_q),
    .in10(register_11_q), .in11(register_12_q), .in12(register_13_q), .in13(register_14_q),
    .in14(register_15_q), .in15(register_16_q), .out(Data1), .sel(RegSelect));  // open: en
  Multiplexer #(.select(4), .width(16)) multiplexer_2 (
    .in0(register_1_q), .in1(register_2_q), .in2(register_3_q), .in3(register_4_q), .in4(register_5_q),
    .in5(register_6_q), .in6(register_7_q), .in7(register_8_q), .in8(register_9_q), .in9(register_10_q),
    .in10(register_11_q), .in11(register_12_q), .in12(register_13_q), .in13(register_14_q),
    .in14(register_15_q), .in15(register_16_q), .out(Data2), .sel(RegTelect));  // open: en

  // Other names for the same wires on the sheet: RS[3:0] = RegSelect; RT[3:0] = RegTelect
endmodule

module ROM (
  input  [15:0] Address,
  input  jump,
  input  clk,
  input  clr,
  output [15:0] Instruction
);

  wire [15:0] adder_1_out, multiplexer_1_out, PC_q;

  Multiplexer #(.width(16)) multiplexer_1 (
    .in0(adder_1_out), .in1(Address), .out(multiplexer_1_out), .sel(jump));  // open: en
  Register #(.width(16)) PC (.D(multiplexer_1_out), .Q(PC_q), .clk(clk), .clr(clr));  // open: en
  Adder #(.width(16)) adder_1 (.a(16'h1), .b(PC_q), .out(adder_1_out));  // open: cin, cout
  ROM_part #(.addrWidth(16), .dataWidth(16)) rom_1 (.addr(PC_q), .data(Instruction));  // open: sel

  // Notes on the sheet:
  //   contents of rom_1 (hex, n*v repeats v):
  //   b201 d003 d000
endmodule

// MEM
module RAM (
  input  [15:0] Address,
  input  [15:0] DataIn,
  input  sw,
  input  clk,
  input  lw,
  input  clr,
  output [15:0] DataOut
);

  RAM_part #(.addrWidth(16), .dataWidth(16), .bus("separate")) ram_1 (
    .addr(Address), .din(DataIn), .data(DataOut), .str(sw), .sel(1'b1), .clk(clk), .ld(lw), .clr(clr));
endmodule

module Control_Logic_2 (
  input  [3:0] OP,
  output ldMem,
  output strMem,
  output strReg,
  output branch,
  output jump,
  output [2:0] ALUOP
);

  wire and_1_out, and_2_out, and_3_out, and_4_out, and_6_out, and_7_out, and_8_out, and_9_out, and_10_out,
       and_11_out, and_12_out, and_13_out, and_14_out, and_15_out, and_16_out, and_17_out, and_18_out,
       and_19_out, not_1_out, not_2_out, not_3_out, not_4_out, not_5_out, not_6_out, not_7_out, not_8_out,
       not_9_out, not_10_out, not_11_out, not_12_out, not_13_out, not_14_out, not_15_out, not_16_out,
       not_17_out, not_18_out;

  not not_1 (not_1_out, OP[2]);
  not not_2 (not_2_out, OP[1]);
  not not_3 (not_3_out, OP[0]);
  not not_4 (not_4_out, OP[3]);
  not not_5 (not_5_out, OP[3]);
  not not_6 (not_6_out, OP[3]);
  not not_7 (not_7_out, OP[2]);
  not not_8 (not_8_out, OP[1]);
  not not_9 (not_9_out, OP[0]);
  and and_1 (and_1_out, OP[3], OP[1], OP[0]);
  and and_2 (and_2_out, OP[3], OP[2]);
  not not_10 (not_10_out, OP[2]);
  not not_11 (not_11_out, OP[1]);
  not not_12 (not_12_out, OP[0]);
  not not_13 (not_13_out, OP[1]);
  not not_14 (not_14_out, OP[0]);
  not not_15 (not_15_out, OP[3]);
  not not_16 (not_16_out, OP[0]);
  not not_17 (not_17_out, OP[1]);
  not not_18 (not_18_out, OP[0]);
  and and_3 (and_3_out, OP[3], not_1_out, not_2_out, OP[0]);
  and and_4 (and_4_out, OP[3], OP[2], OP[1]);
  and and_5 (strMem, OP[3], OP[1], not_3_out);
  and and_6 (and_6_out, not_4_out, OP[0]);
  and and_7 (and_7_out, not_5_out, OP[1]);
  and and_8 (and_8_out, not_6_out, OP[2]);
  and and_9 (and_9_out, OP[3], not_7_out, not_8_out);
  and and_10 (and_10_out, OP[3], OP[1], OP[0]);
  and and_11 (and_11_out, OP[3], OP[2], not_9_out);
  or or_1 (jump, and_1_out, and_2_out);
  and and_12 (and_12_out, not_10_out, not_11_out, not_12_out);
  and and_13 (and_13_out, OP[2], OP[0]);
  and and_14 (and_14_out, OP[2], OP[1]);
  and and_15 (and_15_out, not_13_out, not_14_out);
  and and_16 (and_16_out, OP[1], OP[0]);
  and and_17 (and_17_out, not_15_out, not_16_out);
  and and_18 (and_18_out, not_17_out, not_18_out);
  and and_19 (and_19_out, OP[3], OP[1], OP[0]);
  or or_2 (ldMem, and_3_out, and_4_out);
  or or_3 (strReg, and_6_out, and_7_out, and_8_out, and_9_out);
  or or_4 (branch, and_10_out, and_11_out);
  or or_5 (ALUOP[0], and_12_out, and_13_out, and_14_out);
  or or_6 (ALUOP[1], and_15_out, and_16_out, OP[3]);
  or or_7 (ALUOP[2], and_17_out, and_18_out, and_19_out);
endmodule
