// Logisim project sketch_16xBreno.circ as structural Verilog
module CPU (
);

  wire undriven, undriven_2, undriven_4;
  wire [3:0] rom_1_instruction, rom_1_instruction_2, rom_1_instruction_3, rom_1_instruction_4, undriven_3;
  wire [15:0] alu_1_dataout, multiplexer_1_out, ram_1_dataout, regs_1_data1, regs_1_data2;

  ROM rom_1 (.Instruction({rom_1_instruction_4, rom_1_instruction_3, rom_1_instruction_2, rom_1_instruction}));  // open: Address, jump, clk, clr
  Control_Logic control_logic_1 ();
  Regs regs_1 (
    .RegSelect(rom_1_instruction_2), .RegTelect(rom_1_instruction_3), .RedDest(rom_1_instruction_4),
    .DataIn(multiplexer_1_out), .Data1(regs_1_data1), .Data2(regs_1_data2), .str(undriven), .clk(undriven_2),
    .clr(undriven_4));
  ALU alu_1 (.Data1(regs_1_data1), .Data2(regs_1_data2), .DataOut(alu_1_dataout), .ALUOp(undriven_3));  // open: Zero
  RAM ram_1 (.DataOut(ram_1_dataout));  // open: clr, lw, sw, Address, DataIn
  Multiplexer #(.width(16)) multiplexer_1 (
    .in0(ram_1_dataout), .in1(alu_1_dataout), .out(multiplexer_1_out));  // open: sel, en
endmodule

module ALU (
  input  [3:0] ALUOp,
  input  [15:0] Data1,
  input  [15:0] Data2,
  output Zero,
  output [15:0] DataOut
);
endmodule

module Regs (
  input  [3:0] RegSelect,
  input  str,
  input  [3:0] RegTelect,
  input  [3:0] RedDest,
  input  [15:0] DataIn,
  input  clk,
  input  clr,
  output [15:0] Data1,
  output [15:0] Data2
);

  wire demultiplexer_1_out0, demultiplexer_1_out1, demultiplexer_1_out2, demultiplexer_1_out3,
       demultiplexer_1_out4, demultiplexer_1_out5, demultiplexer_1_out6, demultiplexer_1_out7,
       demultiplexer_1_out8, demultiplexer_1_out9, demultiplexer_1_out10, demultiplexer_1_out11,
       demultiplexer_1_out12, demultiplexer_1_out13, demultiplexer_1_out14, demultiplexer_1_out15;
  wire [15:0] demultiplexer_2_out0, demultiplexer_2_out1, demultiplexer_2_out2, demultiplexer_2_out3,
       demultiplexer_2_out4, demultiplexer_2_out5, demultiplexer_2_out6, demultiplexer_2_out7,
       demultiplexer_2_out8, demultiplexer_2_out9, demultiplexer_2_out10, demultiplexer_2_out11,
       demultiplexer_2_out12, demultiplexer_2_out13, demultiplexer_2_out14, demultiplexer_2_out15,
       register_1_q, register_2_q, register_3_q, register_4_q, register_5_q, register_6_q, register_7_q,
       register_8_q, register_9_q, register_10_q, register_11_q, register_12_q, register_13_q, register_14_q,
       register_15_q, register_16_q;

  Demultiplexer #(.select(4)) demultiplexer_1 (
    .out0(demultiplexer_1_out0), .out1(demultiplexer_1_out1), .out2(demultiplexer_1_out2),
    .out3(demultiplexer_1_out3), .out4(demultiplexer_1_out4), .out5(demultiplexer_1_out5),
    .out6(demultiplexer_1_out6), .out7(demultiplexer_1_out7), .out8(demultiplexer_1_out8),
    .out9(demultiplexer_1_out9), .out10(demultiplexer_1_out10), .out11(demultiplexer_1_out11),
    .out12(demultiplexer_1_out12), .out13(demultiplexer_1_out13), .out14(demultiplexer_1_out14),
    .out15(demultiplexer_1_out15), .in(str), .sel(RedDest), .en(1'b1));
  Demultiplexer #(.select(4), .width(16)) demultiplexer_2 (
    .out0(demultiplexer_2_out0), .out1(demultiplexer_2_out1), .out2(demultiplexer_2_out2),
    .out3(demultiplexer_2_out3), .out4(demultiplexer_2_out4), .out5(demultiplexer_2_out5),
    .out6(demultiplexer_2_out6), .out7(demultiplexer_2_out7), .out8(demultiplexer_2_out8),
    .out9(demultiplexer_2_out9), .out10(demultiplexer_2_out10), .out11(demultiplexer_2_out11),
    .out12(demultiplexer_2_out12), .out13(demultiplexer_2_out13), .out14(demultiplexer_2_out14),
    .out15(demultiplexer_2_out15), .in(DataIn), .sel(RedDest), .en(1'b1));
  Register #(.width(16)) register_1 (
    .D(demultiplexer_2_out0), .en(demultiplexer_1_out0), .Q(register_1_q), .clk(clk), .clr(clr));
  Register #(.width(16)) register_2 (
    .D(demultiplexer_2_out1), .en(demultiplexer_1_out1), .Q(register_2_q), .clk(clk), .clr(clr));
  Register #(.width(16)) register_3 (
    .D(demultiplexer_2_out2), .en(demultiplexer_1_out2), .Q(register_3_q), .clk(clk), .clr(clr));
  Register #(.width(16)) register_4 (
    .D(demultiplexer_2_out3), .en(demultiplexer_1_out3), .Q(register_4_q), .clk(clk), .clr(clr));
  Register #(.width(16)) register_5 (
    .D(demultiplexer_2_out4), .en(demultiplexer_1_out4), .Q(register_5_q), .clk(clk), .clr(clr));
  Register #(.width(16)) register_6 (
    .D(demultiplexer_2_out5), .en(demultiplexer_1_out5), .Q(register_6_q), .clk(clk), .clr(clr));
  Register #(.width(16)) register_7 (
    .D(demultiplexer_2_out6), .en(demultiplexer_1_out6), .Q(register_7_q), .clk(clk), .clr(clr));
  Register #(.width(16)) register_8 (
    .D(demultiplexer_2_out7), .en(demultiplexer_1_out7), .Q(register_8_q), .clk(clk), .clr(clr));
  Register #(.width(16)) register_9 (
    .D(demultiplexer_2_out8), .en(demultiplexer_1_out8), .Q(register_9_q), .clk(clk), .clr(clr));
  Register #(.width(16)) register_10 (
    .D(demultiplexer_2_out9), .en(demultiplexer_1_out9), .Q(register_10_q), .clk(clk), .clr(clr));
  Register #(.width(16)) register_11 (
    .D(demultiplexer_2_out10), .en(demultiplexer_1_out10), .Q(register_11_q), .clk(clk), .clr(clr));
  Register #(.width(16)) register_12 (
    .D(demultiplexer_2_out11), .en(demultiplexer_1_out11), .Q(register_12_q), .clk(clk), .clr(clr));
  Register #(.width(16)) register_13 (
    .D(demultiplexer_2_out12), .en(demultiplexer_1_out12), .Q(register_13_q), .clk(clk), .clr(clr));
  Register #(.width(16)) register_14 (
    .D(demultiplexer_2_out13), .en(demultiplexer_1_out13), .Q(register_14_q), .clk(clk), .clr(clr));
  Register #(.width(16)) register_15 (
    .D(demultiplexer_2_out14), .en(demultiplexer_1_out14), .Q(register_15_q), .clk(clk), .clr(clr));
  Register #(.width(16)) register_16 (
    .D(demultiplexer_2_out15), .en(demultiplexer_1_out15), .Q(register_16_q), .clk(clk), .clr(clr));
  Multiplexer #(.select(4), .width(16)) multiplexer_1 (
    .in0(register_1_q), .in1(register_2_q), .in2(register_3_q), .in3(register_4_q), .in4(register_5_q),
    .in5(register_6_q), .in6(register_7_q), .in7(register_8_q), .in8(register_9_q), .in9(register_10_q),
    .in10(register_11_q), .in11(register_12_q), .in12(register_13_q), .in13(register_14_q),
    .in14(register_15_q), .in15(register_16_q), .out(Data1), .sel(RegSelect), .en(1'b1));
  Multiplexer #(.select(4), .width(16)) multiplexer_2 (
    .in0(register_1_q), .in1(register_2_q), .in2(register_3_q), .in3(register_4_q), .in4(register_5_q),
    .in5(register_6_q), .in6(register_7_q), .in7(register_8_q), .in8(register_9_q), .in9(register_10_q),
    .in10(register_11_q), .in11(register_12_q), .in12(register_13_q), .in13(register_14_q),
    .in14(register_15_q), .in15(register_16_q), .out(Data2), .sel(RegTelect), .en(1'b1));

  // Other names for the same wires on the sheet: RS[3:0] = RegSelect; RT[3:0] = RegTelect
endmodule

module ROM (
  input  [15:0] Address,
  input  jump,
  input  clk,
  input  clr,
  output [15:0] Instruction
);

  wire [15:0] adder_1_out, multiplexer_1_out, PC_q;

  Multiplexer #(.width(16)) multiplexer_1 (
    .in0(adder_1_out), .in1(Address), .out(multiplexer_1_out), .sel(jump));  // open: en
  Register #(.width(16)) PC (.D(multiplexer_1_out), .Q(PC_q), .clk(clk), .clr(clr));  // open: en
  Adder #(.width(16)) adder_1 (.a(16'h1), .b(PC_q), .out(adder_1_out));  // open: cin, cout
  ROM_part #(.addrWidth(16), .dataWidth(16)) rom_1 (.addr(PC_q), .data(Instruction));  // open: sel

  // Notes on the sheet:
  //   contents of rom_1 (hex, n*v repeats v):
  //   111 0 44
endmodule

// MEM
module RAM (
  input  [15:0] Address,
  input  [15:0] DataIn,
  input  sw,
  input  lw,
  input  clr,
  output [15:0] DataOut
);

  wire clock_1_out;

  Clock clock_1 (.out(clock_1_out));
  RAM_part #(.addrWidth(16), .dataWidth(16), .bus("separate")) ram_1 (
    .addr(Address), .din(DataIn), .data(DataOut), .str(sw), .sel(1'b1), .clk(clock_1_out), .ld(lw), .clr(clr));
endmodule
